// Logisim project Logisim Discussion Forum 1.circ as structural Verilog: 1 circuit, main circuit main
// Carry0
module main (
  input  A0,
  input  B0,
  input  A1,
  input  B1,
  output C0,
  output C_out,
  output C1
);

  wire and_1_out, Carry0_out, Carry1_out, S1_out;

  and Carry0 (Carry0_out, A0, B0);
  xor xor_1 (C0, B0, A0);
  and and_1 (and_1_out, A1, B1);
  xor S1 (S1_out, B1, A1);
  xor xor_2 (C1, Carry0_out, S1_out);
  and Carry1 (Carry1_out, Carry0_out, S1_out);
  or or_1 (C_out, Carry1_out, and_1_out);
endmodule
